# Fritzing sketch CircuitPython Fancy LED (saved by Fritzing 0.9.3b)
breadboards: 1

parts:
  Part1 = Adafruit Metro M0 Express
  LED6 = LED - 5mm [color="Green (555nm)" package="5 mm [THT]"]
  R1 = Resistor [tolerance=±5% resistance=220 package="2512 [SMD]"]
  LED7 = LED - 5mm [color="Green (555nm)" package="5 mm [THT]"]
  R2 = Resistor [tolerance=±5% resistance=220 package="2512 [SMD]"]
  LED8 = LED - 5mm [color="Green (555nm)" package="5 mm [THT]"]
  R3 = Resistor [tolerance=±5% resistance=220 package="2512 [SMD]"]
  LED9 = LED - 5mm [color="Green (555nm)" package="5 mm [THT]"]
  R4 = Resistor [tolerance=±5% resistance=220 package="2512 [SMD]"]
  LED10 = LED - 5mm [color="Green (555nm)" package="5 mm [THT]"]
  R5 = Resistor [tolerance=±5% resistance=220 package="2512 [SMD]"]
  LED11 = LED - 5mm [color="Green (555nm)" package="5 mm [THT]"]
  R6 = Resistor [tolerance=±5% resistance=220 package="2512 [SMD]"]
  LED12 = LED - 5mm [color="Green (555nm)" package="5 mm [THT]"]
  R7 = Resistor [tolerance=±5% resistance=220 package="2512 [SMD]"]

nets:
  N1: Part1.D7, R7.Pin_1
  N2: Part1.D6, R6.Pin_1
  N3: Part1.D5, R5.Pin_1
  N4: Part1.D4, R4.Pin_1
  N5: Part1.D3, R3.Pin_1
  N6: Part1.D2, R2.Pin_1
  N7: Part1.D1, R1.Pin_1
  N8: Part1.VIN, LED6.cathode, LED7.cathode, LED8.cathode, LED9.cathode, LED10.cathode, LED11.cathode, LED12.cathode
  N9: LED6.anode, R1.Pin_0
  N10: LED7.anode, R2.Pin_0
  N11: LED8.anode, R3.Pin_0
  N12: LED9.anode, R4.Pin_0
  N13: LED10.anode, R5.Pin_0
  N14: LED11.anode, R6.Pin_0
  N15: LED12.anode, R7.Pin_0

custom parts:
  Adafruit Metro M0 Express: Metro is our series of microcontroller boards for use with the Arduino IDE. This new Metro board looks a whole lot like our original Metro 328, but with a huge upgrade. Instead of the ATmega328, this Metro features a ATSAMD21G18 chip, an ARM Cortex M0+. It's our first Metro that is designed for use with CircuitPython! CircuitPython is our beginner-oriented flavor of MicroPython - and as the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
