# Fritzing sketch CircuitPython LCD (saved by Fritzing 0.9.3b)
breadboards: 1

parts:
  Part1 = Adafruit Metro M0 Express
  S1 = Pushbutton [package="[THT]"]
  S2 = SPST Switch [package=switch-spdt]
  LCD_Backpack1 = LCD Backpack [part_number="LCM1602 IIC" chip_label="LCM1602 IIC" package="DIP (Dual Inline) [THT]"]

nets:
  N1: Part1.SCL, LCD_Backpack1.SCL
  N2: Part1.SDA, LCD_Backpack1.SDA
  GND: Part1.GND, S1.Pin_3, S1.Pin_4, S2.O, LCD_Backpack1.GND
  N3: Part1.D2, S2.S
  N4: Part1.D0, S1.Pin_1, S1.Pin_2
  +5V: Part1.+5V, LCD_Backpack1.VCC

custom parts:
  Adafruit Metro M0 Express: Metro is our series of microcontroller boards for use with the Arduino IDE. This new Metro board looks a whole lot like our original Metro 328, but with a huge upgrade. Instead of the ATmega328, this Metro features a ATSAMD21G18 chip, an ARM Cortex M0+. It's our first Metro that is designed for use with CircuitPython! CircuitPython is our beginner-oriented flavor of MicroPython - and as the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
  LCD Backpack: I2C-Module to use a 1602 or 2004 LCD on with the wire.h library Serial LCD Modul
