# Fritzing sketch CircuitPython Photointerrupters (saved by Fritzing 0.9.3b)
breadboards: 1

parts:
  Part1 = Adafruit Metro M0 Express
  U1 = Photointerrupter [package=cnz1120]

nets:
  N1: Part1.GND, U1.2
  N2: Part1.D2, U1.1
  N3: Part1.+5V, U1.3, U1.4

custom parts:
  Adafruit Metro M0 Express: Metro is our series of microcontroller boards for use with the Arduino IDE. This new Metro board looks a whole lot like our original Metro 328, but with a huge upgrade. Instead of the ATmega328, this Metro features a ATSAMD21G18 chip, an ARM Cortex M0+. It's our first Metro that is designed for use with CircuitPython! CircuitPython is our beginner-oriented flavor of MicroPython - and as the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
  Photointerrupter: LED-to-NPN optoisolator
