# Fritzing sketch CircuitPython RGB (saved by Fritzing 0.9.3b)
breadboards: 1

parts:
  LED1 = RGB LED (com. cathode, rbg) [package="5 mm [THT]"]
  LED2 = RGB LED (com. cathode, rbg) [package="5 mm [THT]"]
  Part1 = Adafruit Metro M0 Express
  R1 = Resistor [tolerance=±5% resistance=220 package="2512 [SMD]"]
  R2 = Resistor [tolerance=±5% resistance=220 package="2512 [SMD]"]

nets:
  N1: LED1.red_anode, Part1.D11
  N2: LED1.common_cathode, R2.Pin_0
  N3: LED1.blue_anode, Part1.D12
  N4: LED1.green_anode, Part1.D13
  N5: LED2.red_anode, Part1.D3
  N6: LED2.common_cathode, R1.Pin_0
  N7: LED2.blue_anode, Part1.D4
  N8: LED2.green_anode, Part1.D5
  N9: Part1.+5V, R1.Pin_1, R2.Pin_1

custom parts:
  Adafruit Metro M0 Express: Metro is our series of microcontroller boards for use with the Arduino IDE. This new Metro board looks a whole lot like our original Metro 328, but with a huge upgrade. Instead of the ATmega328, this Metro features a ATSAMD21G18 chip, an ARM Cortex M0+. It's our first Metro that is designed for use with CircuitPython! CircuitPython is our beginner-oriented flavor of MicroPython - and as the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
